# Fritzing sketch mosfet (saved by Fritzing 0.9.3b)
breadboards: 1

parts:
  FR024N = Basic FET N-Channel [package="DPak [SMD]"]
  354T = Sharp PC817 [package=THT]
  R1 = Resistor [tolerance=±5% resistance=4.7k package=THT]
  LED1 = LED - 5mm [color="Red (633nm)" package="5 mm [THT]"]
  R2 = Resistor [tolerance=±5% resistance=0 package=THT]
  D1 = Rectifier Diode [part_number=1N4148WT package="300 mil [THT]"]
  L1 = Solenoid
  R3 = Resistor [tolerance=±5% resistance=3.3k package=THT]
  LED2 = LED - 5mm [color="Red (633nm)" package="5 mm [THT]"]
  J1 = female pin header, 1 pin [form="♀ (female)"]

nets:
  N1: FR024N.Gate, 354T.Pin_3, R1.Pin_0
  N2: FR024N.drain, D1.anode, L1.pin2
  GND: FR024N.source, 354T.Pin_2, LED1.cathode, R3.Pin_0, R3.Pin_1
  N3: 354T.Pin_1, LED2.cathode
  N4: 354T.Pin_4, R2.Pin_1
  N5: R1.Pin_1, LED1.anode
  12V: R2.Pin_0, D1.cathode, L1.pin1
  N6: LED2.anode, J1.pin1
